// Digital circuit controller.dig as structural Verilog
module controller (
  input  clk,
  input  rst,
  input  beginn,
  input  reset,
  input  zero,
  input  endd,
  output start,
  output load,
  output countdown
);

  wire not_1_out, or_1_out, xor_1_out;

  not not_1 (not_1_out, rst);
  xor xor_1 (xor_1_out, zero, reset);
  or or_1 (or_1_out, not_1_out, reset, xor_1_out);
  JK_FF jk_ff_1 (.J(beginn), .C(clk), .K(or_1_out), .Q(start));  // open: nQ

  assign countdown = endd;
  assign load = reset;
endmodule
