// Digital circuit downcounter.dig as structural Verilog
module downcounter (
  input  rst,
  input  count,
  input  load,
  input  [3:0] pm10,
  input  [3:0] pm1,
  input  [3:0] ps10,
  input  [3:0] ps1,
  input  c1khz,
  output [3:0] s1,
  output [3:0] s10,
  output [3:0] m1,
  output [3:0] m10,
  output zero
);

  wire and_2_out, downcounter_new_1_zero, downcounter_new_2_zero, downcounter_new_3_zero,
       downcounter_new_4_zero, not_1_out, or_1_out, or_2_out, or_3_out, or_4_out, or_5_out, or_6_out;
  wire [3:0] multiplexer_1_out, multiplexer_2_out, multiplexer_3_out, multiplexer_4_out, multiplexer_5_out,
       multiplexer_6_out, multiplexer_7_out, multiplexer_8_out;

  or or_1 (or_1_out, downcounter_new_1_zero, or_6_out);
  downcounter_new downcounter_new_1 (
    .EN(downcounter_new_2_zero), .LOAD(or_1_out), .IN(multiplexer_1_out), .CLK(or_5_out), .RESET(1'b1),
    .CNT(m10), .ZERO(downcounter_new_1_zero));
  Multiplexer #(.Bits(4)) multiplexer_1 (
    .sel(or_6_out), .in_0(4'b1001), .in_1(multiplexer_2_out), .out(multiplexer_1_out));
  Multiplexer #(.Bits(4)) multiplexer_2 (.sel(not_1_out), .in_0(pm10), .in_1(4'b0000), .out(multiplexer_2_out));
  downcounter_new downcounter_new_2 (
    .EN(downcounter_new_3_zero), .LOAD(or_2_out), .IN(multiplexer_3_out), .CLK(or_5_out), .RESET(1'b1),
    .CNT(m1), .ZERO(downcounter_new_2_zero));
  or or_2 (or_2_out, downcounter_new_2_zero, or_6_out);
  Multiplexer #(.Bits(4)) multiplexer_3 (
    .sel(or_6_out), .in_0(4'b1001), .in_1(multiplexer_4_out), .out(multiplexer_3_out));
  Multiplexer #(.Bits(4)) multiplexer_4 (.sel(not_1_out), .in_0(pm1), .in_1(4'b0000), .out(multiplexer_4_out));
  downcounter_new downcounter_new_3 (
    .EN(downcounter_new_4_zero), .LOAD(or_3_out), .IN(multiplexer_5_out), .CLK(or_5_out), .RESET(1'b1),
    .CNT(s10), .ZERO(downcounter_new_3_zero));
  or or_3 (or_3_out, downcounter_new_3_zero, or_6_out);
  Multiplexer #(.Bits(4)) multiplexer_5 (
    .sel(or_6_out), .in_0(4'b0101), .in_1(multiplexer_6_out), .out(multiplexer_5_out));
  downcounter_new downcounter_new_4 (
    .EN(1'b1), .LOAD(or_4_out), .IN(multiplexer_7_out), .CLK(or_5_out), .RESET(1'b1), .CNT(s1),
    .ZERO(downcounter_new_4_zero));
  or or_4 (or_4_out, downcounter_new_4_zero, or_6_out);
  Multiplexer #(.Bits(4)) multiplexer_6 (.sel(not_1_out), .in_0(ps10), .in_1(4'b0000), .out(multiplexer_6_out));
  Multiplexer #(.Bits(4)) multiplexer_7 (
    .sel(or_6_out), .in_0(4'b1001), .in_1(multiplexer_8_out), .out(multiplexer_7_out));
  Multiplexer #(.Bits(4)) multiplexer_8 (.sel(not_1_out), .in_0(ps1), .in_1(4'b0000), .out(multiplexer_8_out));
  and and_1 (zero, downcounter_new_4_zero, downcounter_new_1_zero, downcounter_new_2_zero, downcounter_new_3_zero);
  or or_5 (or_5_out, and_2_out, count);
  and and_2 (and_2_out, or_6_out, c1khz);
  or or_6 (or_6_out, not_1_out, load);
  not not_1 (not_1_out, rst);
endmodule
